# Fritzing sketch 02 (saved by Fritzing 0.9.3b)
breadboards: 1

parts:
  R1 = Resistor [tolerance=±5% resistance=200 package=THT]
  LED1 = LED - 5mm [color="Red (633nm)" package="5 mm [THT]"]
  R7 = Resistor [tolerance=±5% resistance=200 package=THT]
  R8 = Resistor [tolerance=±5% resistance=200 package=THT]
  R9 = Resistor [tolerance=±5% resistance=200 package=THT]
  R10 = Resistor [tolerance=±5% resistance=200 package=THT]
  R11 = Resistor [tolerance=±5% resistance=200 package=THT]
  LED7 = LED - 5mm [color="Red (633nm)" package="5 mm [THT]"]
  LED8 = LED - 5mm [color="Red (633nm)" package="5 mm [THT]"]
  LED9 = LED - 5mm [color="Red (633nm)" package="5 mm [THT]"]
  LED10 = LED - 5mm [color="Red (633nm)" package="5 mm [THT]"]
  LED11 = LED - 5mm [color="Red (633nm)" package="5 mm [THT]"]

nets:
  N1: R1.Pin_0, LED1.cathode
  GND: R1.Pin_1, R7.Pin_1, R8.Pin_1, R9.Pin_1, R10.Pin_1, R11.Pin_1
  Arduino GPIO4: LED1.anode
  N2: R7.Pin_0, LED7.cathode
  N3: R8.Pin_0, LED8.cathode
  N4: R9.Pin_0, LED9.cathode
  N5: R10.Pin_0, LED10.cathode
  N6: R11.Pin_0, LED11.cathode
  Arduino GPIO6: LED7.anode
  Arduino GPIO5: LED8.anode
  Arduino GPIO7: LED9.anode
  Arduino GPIO8: LED10.anode
  Arduino GPIO9: LED11.anode
