# Fritzing sketch 03 (saved by Fritzing 0.9.3b)
breadboards: 1

parts:
  R11 = Resistor [tolerance=±5% resistance=200 package=THT]
  LED11 = LED - 5mm [color="Red (633nm)" package="5 mm [THT]"]
  Potentiometer = Trimmer Potentiometer [maximum_resistance=10kΩ package=THT]

nets:
  N1: R11.Pin_0, LED11.cathode
  GND: R11.Pin_1, Potentiometer.leg2
  Arduino GPIO9: LED11.anode
  5V: Potentiometer.leg1
  Arduino A0: Potentiometer.wiper
