# Fritzing sketch 04 (saved by Fritzing 0.9.3b)
breadboards: 1

parts:
  R12 = Resistor [tolerance=±5% resistance=51k package=THT]
  5_1k = Resistor [tolerance=±5% resistance=200 package=THT]
  Push_Button = Momentary Switch [package=tactile-pth]
  C2 = Ceramic Capacitor [capacitance=100nF package="100 mil [THT, multilayer]"]
  R14 = Resistor [tolerance=±5% resistance=200 package=THT]
  R15 = Resistor [tolerance=±5% resistance=200 package=THT]
  R16 = Resistor [tolerance=±5% resistance=200 package=THT]
  LED12 = LED - 5mm [color="Red (633nm)" package="5 mm [THT]"]
  R17 = Resistor [tolerance=±5% resistance=200 package=THT]
  R18 = Resistor [tolerance=±5% resistance=200 package=THT]
  R19 = Resistor [tolerance=±5% resistance=200 package=THT]
  LED13 = LED - 5mm [color="Red (633nm)" package="5 mm [THT]"]
  LED14 = LED - 5mm [color="Red (633nm)" package="5 mm [THT]"]
  LED15 = LED - 5mm [color="Red (633nm)" package="5 mm [THT]"]
  LED16 = LED - 5mm [color="Red (633nm)" package="5 mm [THT]"]
  LED17 = LED - 5mm [color="Red (633nm)" package="5 mm [THT]"]
  R20 = Resistor [tolerance=±5% resistance=200 package=THT]
  LED18 = LED - 5mm [color="Red (633nm)" package="5 mm [THT]"]

nets:
  5V: R12.Pin_0
  N1: R12.Pin_1, 5_1k.Pin_1, Push_Button.2
  Arduino GPIO2: 5_1k.Pin_0, C2.1
  GND: Push_Button.4, C2.0, R14.Pin_1, R15.Pin_1, R16.Pin_1, R17.Pin_1, R18.Pin_1, R19.Pin_1, R20.Pin_1
  N2: R14.Pin_0, LED13.cathode
  N3: R15.Pin_0, LED12.cathode
  N4: R16.Pin_0, LED14.cathode
  Arduino GPIO4: LED12.anode
  N5: R17.Pin_0, LED15.cathode
  N6: R18.Pin_0, LED16.cathode
  N7: R19.Pin_0, LED17.cathode
  Arduino GPIO6: LED13.anode
  Arduino GPIO5: LED14.anode
  Arduino GPIO7: LED15.anode
  Arduino GPIO8: LED16.anode
  Arduino GPIO9: LED17.anode
  N8: R20.Pin_0, LED18.cathode
  Arduino GPIO13: LED18.anode
