# Fritzing sketch 06 (saved by Fritzing 0.9.3b)
breadboards: 1

parts:
  R1 = Resistor [tolerance=±5% resistance=10k package=THT]
  Photoresistor = Photocell (LDR) [package=THT]

nets:
  GND: R1.Pin_0
  Arduino GPIO2: R1.Pin_1, Photoresistor.pin_0
  5V: Photoresistor.pin_1
