# Fritzing sketch 07 (saved by Fritzing 0.9.3b)
breadboards: 1

parts:
  R4 = Resistor [tolerance=±5% resistance=51k package=THT]
  R5 = Resistor [tolerance=±5% resistance=5.1k package=THT]
  Push_Button = Momentary Switch [package=tactile-pth]
  C2 = Ceramic Capacitor [capacitance=100nF package="100 mil [THT, multilayer]"]
  Buzzer = Piezo Speaker
  R6 = Resistor [tolerance=±5% resistance=100 package=THT]

nets:
  5V: R4.Pin_0
  N1: R4.Pin_1, R5.Pin_1, Push_Button.2
  Arduino GPIO2: R5.Pin_0, C2.1
  GND: Push_Button.4, C2.0, Buzzer.pin2
  N2: Buzzer.pin1, R6.Pin_0
  Arduino GPIO9: R6.Pin_1
