# Fritzing sketch 08 (saved by Fritzing 0.9.3b)
breadboards: 1

parts:
  R4 = Resistor [tolerance=±5% resistance=51k package=THT]
  R5 = Resistor [tolerance=±5% resistance=5.1k package=THT]
  Push_Button = Momentary Switch [package=tactile-pth]
  C2 = Ceramic Capacitor [capacitance=100nF package="100 mil [THT, multilayer]"]
  R7 = Resistor [tolerance=±5% resistance=51k package=THT]
  R8 = Resistor [tolerance=±5% resistance=5.1k package=THT]
  Push_Button_2 = Momentary Switch [package=tactile-pth]
  C3 = Ceramic Capacitor [capacitance=100nF package="100 mil [THT, multilayer]"]
  Standard = Basic Servo
  Submicro = Basic Servo

nets:
  5V: R4.Pin_0, R7.Pin_0, Standard.vcc, Submicro.vcc
  N1: R4.Pin_1, R5.Pin_1, Push_Button.2
  Arduino GPIO2: R5.Pin_0, C2.1
  GND: Push_Button.4, C2.0, Push_Button_2.4, C3.0, Standard.gnd, Submicro.gnd
  N2: R7.Pin_1, R8.Pin_1, Push_Button_2.2
  Arduino GPIO3: R8.Pin_0, C3.1
  Arduino GPIO9: Standard.pulse
  Arduino GPIO10: Submicro.pulse
