# Fritzing sketch 09 (saved by Fritzing 0.9.3b)
breadboards: 1

parts:
  JP1 = Header 4 [package=screwterminal-3.5mm-4_lock]
  Column_Pins = Header 3 [package=jst-3-pth]

nets:
  Arduino GPIO8: JP1.1
  Arduino GPIO7: JP1.2
  Arduino GPIO6: JP1.3
  Arduino GPIO5: JP1.4
  Arduino GPIO4: Column_Pins.1
  Arduino GPIO3: Column_Pins.2
  Arduino GPIO2: Column_Pins.3

notes:
  PIN 1
  PIN 2
  PIN 3
  PIN 4
  PIN 5
  PIN 6
  PIN 7
