# Fritzing sketch 10 (saved by Fritzing 0.9.3b)
breadboards: 1

parts:
  U2 = 74HC595 SMD [package="SO16 [SMD]"]
  R9 = Resistor [tolerance=±5% resistance=200 package=THT]
  R10 = Resistor [tolerance=±5% resistance=200 package=THT]
  R11 = Resistor [tolerance=±5% resistance=200 package=THT]
  R12 = Resistor [tolerance=±5% resistance=200 package=THT]
  R13 = Resistor [tolerance=±5% resistance=200 package=THT]
  R14 = Resistor [tolerance=±5% resistance=200 package=THT]
  R15 = Resistor [tolerance=±5% resistance=200 package=THT]
  R16 = Resistor [tolerance=±5% resistance=200 package=THT]
  LED9 = LED - 5mm [color="Red (633nm)" package="5 mm [THT]"]
  LED10 = LED - 5mm [color="Red (633nm)" package="5 mm [THT]"]
  LED11 = LED - 5mm [color="Red (633nm)" package="5 mm [THT]"]
  LED12 = LED - 5mm [color="Red (633nm)" package="5 mm [THT]"]
  LED13 = LED - 5mm [color="Red (633nm)" package="5 mm [THT]"]
  LED14 = LED - 5mm [color="Red (633nm)" package="5 mm [THT]"]
  LED15 = LED - 5mm [color="Red (633nm)" package="5 mm [THT]"]
  LED16 = LED - 5mm [color="Red (633nm)" package="5 mm [THT]"]

nets:
  N1: U2.Q1, LED11.anode
  N2: U2.Q2, LED12.anode
  N3: U2.Q3, LED10.anode
  N4: U2.Q4, LED14.anode
  N5: U2.Q5, LED13.anode
  N6: U2.Q6, LED16.anode
  N7: U2.Q7, LED15.anode
  GND: U2.GND, U2.OE, R9.Pin_1, R10.Pin_1, R11.Pin_1, R12.Pin_1, R13.Pin_1, R14.Pin_1, R15.Pin_1, R16.Pin_1
  5V: U2.MR, U2.VCC
  Arduino GPIO6: U2.SH_CP
  Arduino GPIO5: U2.ST_CP
  Arduino GPIO4: U2.DS
  N8: U2.Q0, LED9.anode
  N9: R9.Pin_0, LED9.cathode
  N10: R10.Pin_0, LED11.cathode
  N11: R11.Pin_0, LED10.cathode
  N12: R12.Pin_0, LED12.cathode
  N13: R13.Pin_0, LED13.cathode
  N14: R14.Pin_0, LED14.cathode
  N15: R15.Pin_0, LED15.cathode
  N16: R16.Pin_0, LED16.cathode

notes:
  x
