# Fritzing sketch 11 (saved by Fritzing 0.9.3b)
breadboards: 1

parts:
  Seven_Segment_Display = Header 12 [package=1x12_machine-pin-header_lock.004]
  R1 = Resistor [tolerance=±5% resistance=200 package=THT]
  R2 = Resistor [tolerance=±5% resistance=200 package=THT]
  R3 = Resistor [tolerance=±5% resistance=200 package=THT]
  R4 = Resistor [tolerance=±5% resistance=200 package=THT]
  R5 = Resistor [tolerance=±5% resistance=200 package=THT]
  R6 = Resistor [tolerance=±5% resistance=200 package=THT]
  R7 = Resistor [tolerance=±5% resistance=200 package=THT]
  R8 = Resistor [tolerance=±5% resistance=200 package=THT]

nets:
  N1: Seven_Segment_Display.1, R1.Pin_1
  N2: Seven_Segment_Display.2, R2.Pin_1
  N3: Seven_Segment_Display.3, R3.Pin_1
  N4: Seven_Segment_Display.4, R5.Pin_1
  N5: Seven_Segment_Display.5, R4.Pin_1
  Arduino GPIO2: Seven_Segment_Display.6
  N6: Seven_Segment_Display.7, R8.Pin_1
  Arduino GPIO3: Seven_Segment_Display.8
  Arduino GPIO4: Seven_Segment_Display.9
  N7: Seven_Segment_Display.10, R7.Pin_1
  N8: Seven_Segment_Display.11, R6.Pin_1
  Arduino GPIO5: Seven_Segment_Display.12
  Arduino GPIO6: R1.Pin_0
  Arduino GPIO7: R2.Pin_0
  Arduino GPIO8: R3.Pin_0
  Arduino GPIO10: R4.Pin_0
  Arduino GPIO9: R5.Pin_0
  Arduino GPIO13: R6.Pin_0
  Arduino GPIO12: R7.Pin_0
  Arduino GPIO11: R8.Pin_0

notes:
  D1
  D2
  D3
  D4
  DP
  A
  B
  D
  C
  E
  F
  G
