# Fritzing sketch 01 (saved by Fritzing 0.9.3b)
breadboards: 1

parts:
  R1 = Resistor [tolerance=±5% resistance=200 package=THT]
  LED1 = LED - 5mm [color="Red (633nm)" package="5 mm [THT]"]
  JP1 = Header 1 [package=snap-male]
  JP2 = Header 1 [package=snap-male]
  R2 = Resistor [tolerance=±5% resistance=200 package=THT]
  LED2 = LED - 5mm [color="Red (633nm)" package="5 mm [THT]"]
  R3 = Resistor [tolerance=±5% resistance=200 package=THT]
  LED3 = LED - 5mm [color="Red (633nm)" package="5 mm [THT]"]

nets:
  N1: R1.Pin_0, LED1.cathode
  N2: R1.Pin_1, JP1.1, R2.Pin_1
  PWM S0 SIG: LED1.anode
  GND: JP2.1, R3.Pin_1
  N3: R2.Pin_0, LED2.cathode
  PWM S1 SIG: LED2.anode
  N4: R3.Pin_0, LED3.cathode
  PWM S15 SIG: LED3.anode

notes:
  ...
