# Fritzing sketch 02 (saved by Fritzing 0.9.3b)
breadboards: 1

parts:
  Standard = Basic Servo
  Submicro = Basic Servo

nets:
  PWM S0 GND: Standard.gnd
  PWM S0 Vcc: Standard.vcc
  PWM S0 SIG: Standard.pulse
  PWM S1 GND: Submicro.gnd
  PWM S1 Vcc: Submicro.vcc
  PWM S1 SIG: Submicro.pulse
