# Fritzing sketch 03 (saved by Fritzing 0.9.3b)
breadboards: 1

parts:
  SN754410 = H-Bridge [package=THT]
  DC_Motor = DC Motor
  SPDT1 = Toggle Switch [package=THT]
  SPDT2 = Toggle Switch [package=THT]
  SPDT3 = Toggle Switch [package=THT]

nets:
  PWM S0 Vcc: SN754410.1_2EN, SN754410.VCC2, SPDT1.L1, SPDT2.L1, SPDT3.L1
  PWM S0 SIG: SN754410.1A
  N1: SN754410.1Y, DC_Motor.pin_1
  GND: SN754410.GND1, SN754410.GND2, SN754410.GND3, SN754410.GND4, SPDT1.L2, SPDT2.L2, SPDT3.L2
  N2: SN754410.2Y, DC_Motor.pin_2
  PWM S1 SIG: SN754410.2A
  Expansion GPIO0: SPDT1.COM
  Expansion GPIO1: SPDT2.COM
  Expansion GPIO2: SPDT3.COM
