# Fritzing sketch 07 (saved by Fritzing 0.9.3b)
breadboards: 1

parts:
  SPDT1 = Toggle Switch [package=THT]
  Buzzer = Piezo Speaker
  Relay_CH0 = RELAY [package=OJ]

nets:
  3.3V: SPDT1.L1
  Expansion GPIO0: SPDT1.COM
  GND: SPDT1.L2, Buzzer.pin2
  N1: Buzzer.pin1, Relay_CH0.MAIN
  5V: Relay_CH0.NO
