# Fritzing sketch 02 (saved by Fritzing 0.9.3b)
breadboards: 1

parts:
  R1 = Resistor [tolerance=±5% resistance=200 package=THT]
  LED1 = LED - 5mm [color="Red (633nm)" package="5 mm [THT]"]
  R2 = Resistor [tolerance=±5% resistance=200 package=THT]
  LED2 = LED - 5mm [color="Red (633nm)" package="5 mm [THT]"]
  R3 = Resistor [tolerance=±5% resistance=200 package=THT]
  LED3 = LED - 5mm [color="Red (633nm)" package="5 mm [THT]"]
  R4 = Resistor [tolerance=±5% resistance=200 package=THT]
  R5 = Resistor [tolerance=±5% resistance=200 package=THT]
  R6 = Resistor [tolerance=±5% resistance=200 package=THT]
  LED4 = LED - 5mm [color="Red (633nm)" package="5 mm [THT]"]
  LED5 = LED - 5mm [color="Red (633nm)" package="5 mm [THT]"]
  LED6 = LED - 5mm [color="Red (633nm)" package="5 mm [THT]"]

nets:
  N1: R1.Pin_0, LED1.cathode
  GND: R1.Pin_1, R2.Pin_1, R3.Pin_1, R4.Pin_1, R5.Pin_1, R6.Pin_1
  Expansion GPIO19: LED1.anode
  N2: R2.Pin_0, LED2.cathode
  Expansion GPIO18: LED2.anode
  N3: R3.Pin_0, LED3.cathode
  Expansion GPIO3: LED3.anode
  N4: R4.Pin_0, LED5.cathode
  N5: R5.Pin_0, LED4.cathode
  N6: R6.Pin_0, LED6.cathode
  Expansion GPIO0: LED4.anode
  Expansion GPIO1: LED5.anode
  Expansion GPIO2: LED6.anode
