# Fritzing sketch 04-01 (saved by Fritzing 0.9.3b)
breadboards: 1

parts:
  SPDT_Switch = SWITCH_SPDT [package=kps-1290]
  R1 = Resistor [tolerance=±5% resistance=200 package=THT]
  LED1 = LED - 5mm [color="Red (633nm)" package="5 mm [THT]"]

nets:
  5V: SPDT_Switch.O
  Expansion GPIO0: SPDT_Switch.P
  GND: SPDT_Switch.S, R1.Pin_1
  N1: R1.Pin_0, LED1.cathode
  Expansion GPIO1: LED1.anode
