# Fritzing sketch 04-02 (saved by Fritzing 0.9.3b)
breadboards: 1

parts:
  SPDT_Switch = SWITCH_SPDT [package=kps-1290]
  R1 = Resistor [tolerance=±5% resistance=200 package=THT]
  LED1 = LED - 5mm [color="Red (633nm)" package="5 mm [THT]"]

nets:
  GND: SPDT_Switch.O, R1.Pin_1
  N1: SPDT_Switch.P, LED1.anode
  5V: SPDT_Switch.S
  N2: R1.Pin_0, LED1.cathode
