# Fritzing sketch 05-01 (saved by Fritzing 0.9.3b)
breadboards: 1

parts:
  R1 = Resistor [tolerance=±5% resistance=200 package=THT]
  LED1 = LED - 5mm [color="Red (633nm)" package="5 mm [THT]"]
  S2 = Momentary Switch [package=tactile-pth]

nets:
  N1: R1.Pin_0, LED1.cathode
  GND: R1.Pin_1
  N2: LED1.anode, S2.3
  3.3V: S2.1
