# Fritzing sketch 05-02 (saved by Fritzing 0.9.3b)
breadboards: 1

parts:
  R1 = Resistor [tolerance=±5% resistance=200 package=THT]
  LED1 = LED - 5mm [color="Red (633nm)" package="5 mm [THT]"]
  R4 = Resistor [tolerance=±5% resistance=51k package=THT]
  R5 = Resistor [tolerance=±5% resistance=5.1k package=THT]
  Push_Button1 = Momentary Switch [package=tactile-pth]
  C2 = Ceramic Capacitor [capacitance=100nF package="100 mil [THT, multilayer]"]

nets:
  N1: R1.Pin_0, LED1.cathode
  GND: R1.Pin_1, Push_Button1.4, C2.0
  Expansion GPIO1: LED1.anode
  5V: R4.Pin_0
  N2: R4.Pin_1, R5.Pin_1, Push_Button1.2, C2.1
  Expansion GPIO0: R5.Pin_0
