# Fritzing sketch 06 (saved by Fritzing 0.9.3b)
breadboards: 1

parts:
  R1 = Resistor [tolerance=±5% resistance=200 package=THT]
  LED1 = LED - 5mm [color="Red (633nm)" package="5 mm [THT]"]
  R2 = Resistor [tolerance=±5% resistance=200 package=THT]
  LED2 = LED - 5mm [color="Red (633nm)" package="5 mm [THT]"]
  R3 = Resistor [tolerance=±5% resistance=200 package=THT]
  R4 = Resistor [tolerance=±5% resistance=200 package=THT]
  LED3 = LED - 5mm [color="Red (633nm)" package="5 mm [THT]"]
  LED4 = LED - 5mm [color="Red (633nm)" package="5 mm [THT]"]
  R5 = Resistor [tolerance=±5% resistance=200 package=THT]
  R6 = Resistor [tolerance=±5% resistance=200 package=THT]
  R7 = Resistor [tolerance=±5% resistance=200 package=THT]
  R8 = Resistor [tolerance=±5% resistance=200 package=THT]
  LED5 = LED - 5mm [color="Red (633nm)" package="5 mm [THT]"]
  LED6 = LED - 5mm [color="Red (633nm)" package="5 mm [THT]"]
  LED7 = LED - 5mm [color="Red (633nm)" package="5 mm [THT]"]
  LED8 = LED - 5mm [color="Red (633nm)" package="5 mm [THT]"]
  U1 = 74HC595 SMD [package="SO16 [SMD]"]

nets:
  N1: R1.Pin_0, LED1.cathode
  GND: R1.Pin_1, R2.Pin_1, R3.Pin_1, R4.Pin_1, R5.Pin_1, R6.Pin_1, R7.Pin_1, R8.Pin_1, U1.GND, U1.OE
  N2: LED1.anode, U1.Q6
  N3: R2.Pin_0, LED2.cathode
  N4: LED2.anode, U1.Q7
  N5: R3.Pin_0, LED3.cathode
  N6: R4.Pin_0, LED4.cathode
  N7: LED3.anode, U1.Q4
  N8: LED4.anode, U1.Q5
  N9: R5.Pin_0, LED5.cathode
  N10: R6.Pin_0, LED7.cathode
  N11: R7.Pin_0, LED6.cathode
  N12: R8.Pin_0, LED8.cathode
  N13: LED5.anode, U1.Q2
  N14: LED6.anode, U1.Q1
  N15: LED7.anode, U1.Q3
  N16: LED8.anode, U1.Q0
  3.3V: U1.MR, U1.VCC
  Expansion GPIO2: U1.SH_CP
  Expansion GPIO3: U1.ST_CP
  Expansion GPIO1: U1.DS

notes:
  x
