# Fritzing sketch 07 (saved by Fritzing 0.9.3b)
breadboards: 1

parts:
  U1 = 74HC595 SMD [package="SO16 [SMD]"]
  Seven_Segment_Display = Header 6 [package=1x06_smd_straight_alt]
  JP2 = Header 6 [package=1x06_smd_straight_alt]
  R1 = Resistor [tolerance=±5% resistance=200 package=THT]
  R2 = Resistor [tolerance=±5% resistance=200 package=THT]
  R4 = Resistor [tolerance=±5% resistance=200 package=THT]
  R5 = Resistor [tolerance=±5% resistance=200 package=THT]
  R6 = Resistor [tolerance=±5% resistance=200 package=THT]
  R7 = Resistor [tolerance=±5% resistance=200 package=THT]
  R8 = Resistor [tolerance=±5% resistance=200 package=THT]
  R9 = Resistor [tolerance=±5% resistance=200 package=THT]

nets:
  N1: U1.Q1, R2.Pin_0
  N2: U1.Q2, R4.Pin_0
  N3: U1.Q3, R6.Pin_0
  N4: U1.Q4, R7.Pin_0
  N5: U1.Q5, R8.Pin_0
  N6: U1.Q6, R5.Pin_0
  N7: U1.Q7, R1.Pin_0
  GND: U1.GND, U1.OE
  5V: U1.MR, U1.VCC
  Expansion GPIO2: U1.SH_CP
  Expansion GPIO3: U1.ST_CP
  Expansion GPIO1: U1.DS
  N8: U1.Q0, R9.Pin_0
  N9: Seven_Segment_Display.1, R7.Pin_1
  N10: Seven_Segment_Display.2, R6.Pin_1
  N11: Seven_Segment_Display.3, R1.Pin_1
  N12: Seven_Segment_Display.4, R4.Pin_1
  N13: Seven_Segment_Display.5, R5.Pin_1
  Expansion GPIO0: Seven_Segment_Display.6
  N14: JP2.1, R2.Pin_1
  Expansion GPIO19: JP2.2
  Expansion GPIO18: JP2.3
  N15: JP2.4, R8.Pin_1
  N16: JP2.5, R9.Pin_1
  Expansion GPIO11: JP2.6

notes:
  D1  A   F  D2 D3 B
  E  D Dp C  G D4
  O
