# Fritzing sketch 10 (saved by Fritzing 0.9.3b)
breadboards: 1

parts:
  LCD_Screen = Header 4 [package=molex-1x4_lock]
  DS18B21 = Header 3 [package=jst-3-pth]
  R2 = Resistor [tolerance=±5% resistance=5.1k package=THT]

nets:
  3.3V: LCD_Screen.1, DS18B21.1, R2.Pin_1
  Expansion SDA: LCD_Screen.2
  Expansion SCL: LCD_Screen.3
  GND: LCD_Screen.4, DS18B21.3
  Expansion GPIO19: DS18B21.2, R2.Pin_0

notes:
  SCL
  SDA
  Vcc
  GND
  DQ
  VDD
