# Fritzing sketch debounce (saved by Fritzing 0.9.3b)
breadboards: 1

parts:
  Push_Button = Momentary Switch [package=tactile-pth]
  R2 = Resistor [tolerance=±5% resistance=5.1k package=THT]
  C1 = Ceramic Capacitor [capacitance=100nF package="100 mil [THT, multilayer]"]
  R3 = Resistor [tolerance=±5% resistance=51k package=THT]

nets:
  N1: Push_Button.2, R2.Pin_1, R3.Pin_1
  GND: Push_Button.4, C1.0
  GPIO: R2.Pin_0, C1.1
  5V: R3.Pin_0
